# Fritzing sketch HoerSpielBox (saved by Fritzing 0.9.4)
circuit board: 4.86567cm x 6.36844cm
breadboards: 1

parts:
  Arduino = Arduino Nano (Rev3.0)
  DFPlayer_Mini = DFRobot DFPlayer Mini [part_number=DFR0299]
  1k_Ohm = Resistor [tolerance=±5% resistance=1k package=THT]
  NFC = male pin header, 7 pins [form="♂ (male)"]
  USB = male pin header, 4 pins [form="♂ (male)"]
  VIN = male pin header, 2 pins [form="♂ (male)"]
  DAC = male pin header, 2 pins [form="♂ (male)"]
  Speaker = male pin header, 2 pins [form="♂ (male)"]
  A0 = male pin header, 2 pins [form="♂ (male)"]
  A1 = male pin header, 2 pins [form="♂ (male)"]
  A2 = male pin header, 2 pins [form="♂ (male)"]
  A3 = male pin header, 2 pins [form="♂ (male)"]
  A4 = male pin header, 2 pins [form="♂ (male)"]
  Power = male pin header, 2 pins [form="♂ (male)"]
  A5 = male pin header, 2 pins [form="♂ (male)"]
  A6 = male pin header, 2 pins [form="♂ (male)"]
  D5 = male pin header, 2 pins [form="♂ (male)"]
  D6 = male pin header, 2 pins [form="♂ (male)"]

nets:
  N1: Arduino.GND, DFPlayer_Mini.GND-1, DFPlayer_Mini.GND-2, NFC.pin3, USB.pin4, VIN.pin1, A0.pin1, A1.pin1, A2.pin1, A3.pin1, A4.pin1, Power.pin1, A5.pin1, A6.pin1, D5.pin2, D6.pin2
  N2: Arduino.D2, DFPlayer_Mini.TX
  N3: Arduino.D3, 1k_Ohm.Pin_0
  N4: Arduino.D4, DFPlayer_Mini.BUSY
  N5: Arduino.D5, D5.pin1
  N6: Arduino.D6, D6.pin1
  N7: Arduino.D9, NFC.pin2
  N8: Arduino.D10, NFC.pin7
  N9: Arduino.D11/MOSI, NFC.pin5
  N10: Arduino.D12/MISO, NFC.pin4
  N11: Arduino.VIN, Power.pin2
  5V: Arduino.5V, DFPlayer_Mini.VCC
  N12: Arduino.A6, A6.pin2
  N13: Arduino.A5, A5.pin2
  N14: Arduino.A4, A4.pin2
  N15: Arduino.A3, A3.pin2
  N16: Arduino.A2, A2.pin2
  N17: Arduino.A1, A1.pin2
  N18: Arduino.A0, A0.pin2
  N19: Arduino.3V3, NFC.pin1
  N20: Arduino.D13/SCK, NFC.pin6
  N21: DFPlayer_Mini.RX, 1k_Ohm.Pin_1
  N22: DFPlayer_Mini.DAC_R, DAC.pin2
  N23: DFPlayer_Mini.DAC_L, DAC.pin1
  N24: DFPlayer_Mini.SPK_1, Speaker.pin2
  N25: DFPlayer_Mini.SPK_2, Speaker.pin1
  N26: DFPlayer_Mini.USB_POS, USB.pin2
  N27: DFPlayer_Mini.USB_NEG, USB.pin1
  N28: USB.pin3, VIN.pin2

notes:
  DATA-
  DATA+
  GND
  VIN
  3.3V
  RST
  MISO
  MOSI
  SCK
  SDA
  ANLG
  HoerSpielBox
  Eduard Itrich, Nov. 2020, V.1
  SPK+
  SPK-
  DAC L
  DAC R
  USB
  DIG
